# Fritzing sketch schema_puzzel1 (saved by Fritzing 0.9.4)
breadboards: 1

parts:
  MCU1 = Raspberry Pi Zero
  KEYPAD1 = Membrane Matrix Keypad
  Part1 = RFID-RC522-v2
  J1 = Basic Servo
  Nokia_5110_LCD_Module1 = Nokia 5110 LCD
  J2 = Piezo Speaker

nets:
  3.3V: MCU1.pin_1, MCU1.pin_17, Part1.3.3V, Nokia_5110_LCD_Module1.VCC
  N1: MCU1.pin_2, J1.vcc
  GND: MCU1.pin_6, MCU1.pin_9, MCU1.pin_20, MCU1.pin_39, Part1.GND, J1.gnd, Nokia_5110_LCD_Module1.GND, J2.pin1
  N2: MCU1.pin_7, KEYPAD1.7
  N3: MCU1.pin_8, KEYPAD1.1
  N4: MCU1.pin_10, KEYPAD1.2
  N5: MCU1.pin_11, J1.pulse
  N6: MCU1.pin_12, KEYPAD1.3
  N7: MCU1.pin_15, KEYPAD1.5
  N8: MCU1.pin_16, KEYPAD1.4
  N9: MCU1.pin_18, KEYPAD1.6
  N10: MCU1.pin_19, Part1.MOSI, Nokia_5110_LCD_Module1.Din
  N11: MCU1.pin_21, Part1.MISO
  N12: MCU1.pin_22, Part1.RST
  N13: MCU1.pin_23, Part1.SCK, Nokia_5110_LCD_Module1.CLK
  N14: MCU1.pin_24, Part1.SDA
  N15: MCU1.pin_26, Nokia_5110_LCD_Module1.CE
  N16: MCU1.pin_36, Nokia_5110_LCD_Module1.D/C
  N17: MCU1.pin_37, J2.pin2
  N18: MCU1.pin_38, Nokia_5110_LCD_Module1.RST
  N19: MCU1.pin_40, Nokia_5110_LCD_Module1.BL

custom parts:
  Membrane Matrix Keypad: Membrane Matrix 3x4 Keypad
  RFID-RC522-v2: A simple China made RFID-RC522 Reader; do check the pin labels, as this is a MFRC522 based clone.
  Nokia 5110 LCD: Nokia 5110 Graphic 84*48 LCD module <Blue Version>
